# Fritzing sketch mike_h2_sensors (saved by Fritzing 0.9.5d)
breadboards: 1

parts:
  Part1 = HC-SR501 Body Sensor Module
  HC-SR04_Sensor_1 = HC-SR04 Ultrasonic Distance Sensor  # not connected
  RCWL-0516_Microwave_Radar_Motion_Sensor1 = RCWL-0516 Microwave Radar Motion Sensor Module
  A1 = esp32-h2 supermini tht

nets:
  VCC: Part1.VCC, RCWL-0516_Microwave_Radar_Motion_Sensor1.VIN, A1.Pin_22
  N1: Part1.OUT, A1.Pin_4
  GND: Part1.GND, RCWL-0516_Microwave_Radar_Motion_Sensor1.GND, A1.Pin_21
  N2: RCWL-0516_Microwave_Radar_Motion_Sensor1.OUT, A1.Pin_5

custom parts:
  HC-SR501 Body Sensor Module: Pyroelectric Infrared PIR Motion Sensor Detector Module
  RCWL-0516 Microwave Radar Motion Sensor Module: The RCWL-0516 is a microwave radar motion sensor module. Input voltage is 4V to 28V. The 3V3 pin is a power output.
  esp32-h2 supermini tht: esp32-h2 supermini development board.
