# Fritzing sketch esp32h2_8relays (saved by Fritzing 0.9.5d)
breadboards: 1

parts:
  A1 = esp32-h2 supermini tht
  S1 = Pushbutton [package="[THT]"]

nets:
  N1: A1.Pin_4, A1.Pin_5, A1.Pin_6, A1.Pin_8
  N2: A1.Pin_14, A1.Pin_17, S1.Pin_1, S1.Pin_2, S1.Pin_3, S1.Pin_4
  N3: A1.Pin_15, A1.Pin_16

notes:
  5V|3|5|2|1|0|12|11|10|GND

custom parts:
  esp32-h2 supermini tht: esp32-h2 supermini development board.
